# Fritzing sketch Ballbalancing Robot (saved by Fritzing 0.9.3b)

parts:
  hc-sr1 = hc-sr04
  J1 = Basic Servo
  Part1 = Arduino Uno (Rev3)
  R1 = Rotary Potentiometer (Large) [maximum_resistance=100kΩ package=THT]

nets:
  N1: hc-sr1.Trig, Part1.D9_PWM
  N2: hc-sr1.Echo, Part1.D10_PWM/SS
  N3: J1.pulse, Part1.D8
  N4: Part1.A0, R1.wiper

notes:
  Connect to Common GND
  Connect Arduino's +5V
  Connect to Arduino's 5V
  Connect to Arduino's common GND.
  Connect to Arduino +5V
  Connect to Common GND.
  10K Potentiometer
  Signal Pin to Pin 8 of Arduino
